// Logisim project BUS_74HC125.circ as structural Verilog: 1 circuit, main circuit main
module main (
);

  wire button_1_out, dipswitch_1_sw1, dipswitch_1_sw2, dipswitch_1_sw3, dipswitch_1_sw4, n7404_1_pin2,
       n74125_1_pin3, n74125_1_pin6, n74125_1_pin8, n74125_1_pin11;

  Button button_1 (.out(button_1_out));
  DipSwitch #(.number(4)) dipswitch_1 (
    .sw1(dipswitch_1_sw1), .sw2(dipswitch_1_sw2), .sw3(dipswitch_1_sw3), .sw4(dipswitch_1_sw4));
  _7404 #(.ShowInternalStructure("true")) u_7404_1 (
    .pin1(button_1_out), .pin2(n7404_1_pin2));  // open: pin3, pin4, pin5, pin6, pin13, pin12, pin11, pin10, pin9, pin8
  _74125 #(.ShowInternalStructure("true")) u_74125_1 (
    .pin1(n7404_1_pin2), .pin2(dipswitch_1_sw1), .pin3(n74125_1_pin3), .pin4(n7404_1_pin2),
    .pin5(dipswitch_1_sw2), .pin6(n74125_1_pin6), .pin13(n7404_1_pin2), .pin12(dipswitch_1_sw3),
    .pin11(n74125_1_pin11), .pin10(n7404_1_pin2), .pin9(dipswitch_1_sw4), .pin8(n74125_1_pin8));
  LedBar #(.matrixcols(4)) ledbar_1 (
    .led0(n74125_1_pin3), .led1(n74125_1_pin6), .led2(n74125_1_pin11), .led3(n74125_1_pin8));
endmodule
