// Logisim project Contador_74HC161.circ as structural Verilog: 1 circuit, main circuit main
module main (
);

  wire n74161_1_pin1, n74161_1_pin2, n74161_1_pin3, n74161_1_pin4, n74161_1_pin5, n74161_1_pin6,
       n74161_1_pin9, n74161_1_pin11, n74161_1_pin12, n74161_1_pin13, n74161_1_pin14, n74161_1_pin15;

  _74161 #(.ShowInternalStructure("true")) u_74161_1 (
    .pin1(n74161_1_pin1), .pin2(n74161_1_pin2), .pin3(n74161_1_pin3), .pin4(n74161_1_pin4),
    .pin5(n74161_1_pin5), .pin6(n74161_1_pin6), .pin7(n74161_1_pin1), .pin15(n74161_1_pin15),
    .pin14(n74161_1_pin14), .pin13(n74161_1_pin13), .pin12(n74161_1_pin12), .pin11(n74161_1_pin11),
    .pin10(n74161_1_pin1), .pin9(n74161_1_pin9));
  Clock clock_1 (.out(n74161_1_pin2));
  LED led_1 (.in(n74161_1_pin15));
  LedBar #(.matrixcols(4)) ledbar_1 (
    .led0(n74161_1_pin14), .led1(n74161_1_pin13), .led2(n74161_1_pin12), .led3(n74161_1_pin11));
  DipSwitch #(.number(4)) dipswitch_1 (
    .sw1(n74161_1_pin3), .sw2(n74161_1_pin4), .sw3(n74161_1_pin5), .sw4(n74161_1_pin6));
  Button #(.press("passive")) button_1 (.out(n74161_1_pin9));
  // also tied to VCC on the sheet: n74161_1_pin1
endmodule
